# Fritzing sketch launch computer v1 (saved by Fritzing 0.9.3b)
circuit board: 15cm x 11.5cm
breadboards: 1

parts:
  MBED = mbed
  microSD_Transflash2 = SparkFun - microSD Transflash
  XBee = XBee
  R1 = Resistor [tolerance=±5% resistance=220 package=THT]
  R2 = Resistor [tolerance=±5% resistance=220 package=THT]
  J13 = female pin header, 2 pins [form="♀ (female)"]
  J14 = female pin header, 2 pins [form="♀ (female)"]
  J15 = female pin header, 2 pins [form="♀ (female)"]
  J16 = female pin header, 2 pins [form="♀ (female)"]
  J17 = female pin header, 2 pins [form="♀ (female)"]
  J18 = female pin header, 2 pins [form="♀ (female)"]
  J19 = female pin header, 2 pins [form="♀ (female)"]
  J21 = female pin header, 2 pins [form="♀ (female)"]
  J22 = female pin header, 2 pins [form="♀ (female)"]
  J20 = female pin header, 2 pins [form="♀ (female)"]
  J35 = female pin header, 2 pins [form="♀ (female)"]  # not connected
  J36 = female pin header, 2 pins [form="♀ (female)"]
  J43 = female pin header, 2 pins [form="♀ (female)"]  # not connected
  J45 = female pin header, 2 pins [form="♀ (female)"]  # not connected
  J54 = female pin header, 2 pins [form="♀ (female)"]  # not connected
  J55 = female pin header, 2 pins [form="♀ (female)"]  # not connected
  R3 = Resistor [tolerance=±5% resistance=220 package=THT]
  J61 = Screw terminal - 2 pins [package=THT]
  J62 = Screw terminal - 2 pins [package=THT]
  J63 = female pin header, 2 pins [form="♀ (female)"]  # not connected
  J64 = female pin header, 2 pins [form="♀ (female)"]  # not connected
  J65 = female pin header, 2 pins [form="♀ (female)"]  # not connected
  J66 = female pin header, 2 pins [form="♀ (female)"]  # not connected
  J67 = female pin header, 2 pins [form="♀ (female)"]  # not connected
  J68 = female pin header, 2 pins [form="♀ (female)"]  # not connected

nets:
  GND: MBED.GND, microSD_Transflash2.GND, XBee.GND, J22.pin2, J61.pin1, J62.pin1
  N1: MBED.pin5, microSD_Transflash2.DI
  N2: MBED.pin6, microSD_Transflash2.DO
  N3: MBED.pin7, microSD_Transflash2.SCK
  N4: MBED.pin8, microSD_Transflash2.CS
  N5: MBED.pin9, XBee.pin3
  N6: MBED.pin10, XBee.pin2
  N7: MBED.pin11, XBee.pin5
  N8: MBED.pin12, J22.pin1
  N9: MBED.pin13, J20.pin2
  N10: MBED.pin14, J20.pin1
  N11: MBED.pin15, R1.Pin_0
  N12: MBED.pin16, R2.Pin_0
  N13: MBED.pin17, J14.pin2
  N14: MBED.pin18, J14.pin1
  N15: MBED.pin19, J15.pin2
  N16: MBED.pin20, J15.pin1
  N17: MBED.pin21, J17.pin2
  N18: MBED.pin22, J17.pin1
  N19: MBED.pin23, J13.pin2
  N20: MBED.pin24, J21.pin1
  N21: MBED.pin25, J21.pin2
  N22: MBED.pin26, J18.pin1
  N23: MBED.pin27, J18.pin2
  N24: MBED.pin28, J16.pin1
  N25: MBED.pin29, J16.pin2
  N26: MBED.pin30, J19.pin1
  VCC: MBED.VOUT, microSD_Transflash2.VCC, XBee.VCC, J19.pin2
  N27: J36.pin2, R3.Pin_0

notes:
  27
  26
  25
  24
  23
  22
  21
  28
  VOUT
  19
  17
  18
  20
  14
  13
  12
  VB
  nR
  VIN
  GND
  -LED2+
  -LED1+
  30
  29
  -LED3+
  Charger
  Battery
  LED3
  Switch
  -  +
  - +
  Whitworth
  Launch Computer v.1
  University
  July 2017
  Kevin Teo
  07/19/17
