# Fritzing sketch miniFlightComputerV1 (saved by Fritzing 0.9.3b)
circuit board: 9cm x 6cm

parts:
  MBED = MBED_NXP_LPC1768 [package=dil40_0.9]
  R3 = Resistor [tolerance=±5% resistance=220 package=THT]
  R2 = Resistor [tolerance=±5% resistance=220 package=THT]
  R1 = Resistor [tolerance=±5% resistance=220 package=THT]
  microSD_breakout = SparkFun - microSD Transflash
  Xbee = XBee
  Charger/Battery = screw terminal, 4 pins
  J1 = shrouded pin header, 10 pins [form="♂ (shrouded male)"]
  Terminal_1 = screw terminal, 6 pins
  Terminal_2 = screw terminal, 15 pins

nets:
  GND: MBED.P$1, microSD_breakout.GND, Xbee.GND, Charger/Battery.pin2, Charger/Battery.pin4, J1.pin1, Terminal_1.pin6
  N1: MBED.P$2, J1.pin10
  N2: MBED.P$5, microSD_breakout.DI, Terminal_2.pin15
  N3: MBED.P$6, microSD_breakout.DO, Terminal_2.pin14
  N4: MBED.P$7, microSD_breakout.SCK, Terminal_2.pin13
  N5: MBED.P$8, microSD_breakout.CS
  N6: MBED.P$9, Terminal_2.pin12
  N7: MBED.P$10, Terminal_2.pin11
  N8: MBED.P$11, Terminal_2.pin10
  N9: MBED.P$12, Terminal_2.pin9
  N10: MBED.P$13, Terminal_2.pin8
  N11: MBED.P$14, Terminal_2.pin7
  N12: MBED.P$15, Terminal_2.pin6
  N13: MBED.P$16, Terminal_2.pin5
  N14: MBED.P$17, Terminal_2.pin4
  N15: MBED.P$18, Terminal_2.pin3
  N16: MBED.P$19, Terminal_2.pin2
  N17: MBED.P$20, Terminal_2.pin1
  N18: MBED.P$21, R1.Pin_1
  N19: MBED.P$22, R2.Pin_1
  N20: MBED.P$23, R3.Pin_1
  N21: MBED.P$24, Terminal_1.pin1
  N22: MBED.P$25, Terminal_1.pin2
  N23: MBED.P$26, Xbee.pin5
  N24: MBED.P$27, Xbee.pin3
  N25: MBED.P$28, Xbee.pin2
  N26: MBED.P$29, Terminal_1.pin3
  N27: MBED.P$30, Terminal_1.pin4
  VCC: MBED.P$40, microSD_breakout.VCC, Xbee.VCC, Terminal_1.pin5
  N28: R3.Pin_0, J1.pin4
  N29: R2.Pin_0, J1.pin3
  N30: R1.Pin_0, J1.pin2
  N31: Charger/Battery.pin1, J1.pin6
  N32: Charger/Battery.pin3, J1.pin7

notes:
  5   6   7   9  10  11  12  13  14  15  16  17  18  19  20
  GND VOUT 30  29  25  24
  (-)(+)
  Whitworth University Mini-Flight Computer v.1
  Craig Russell - 06/03/19
  (+) (-) (+) (-)
