# Fritzing sketch FlightComputerV1_2 (saved by Fritzing 0.9.3b)
circuit board: 14cm x 10cm

parts:
  MBED = MBED_NXP_LPC1768 [package=dil40_0.9]
  R3 = Resistor [tolerance=±5% resistance=220 package=THT]
  R2 = Resistor [tolerance=±5% resistance=220 package=THT]
  R1 = Resistor [tolerance=±5% resistance=220 package=THT]
  microSD_breakout = SparkFun - microSD Transflash
  Xbee = XBee
  Charger/Battery = screw terminal, 4 pins
  J1 = shrouded pin header, 10 pins [form="♂ (shrouded male)"]
  J2 = screw terminal, 16 pins
  J3 = screw terminal, 16 pins
  Analog = female pin header, 2 pins [form="♀ (female)"]
  Analog_2 = female pin header, 2 pins [form="♀ (female)"]
  CAN = female pin header, 2 pins [form="♀ (female)"]
  I2C = female pin header, 2 pins [form="♀ (female)"]
  GPIO = female pin header, 2 pins [form="♀ (female)"]
  Analog_3 = female pin header, 2 pins [form="♀ (female)"]
  Serial = female pin header, 2 pins [form="♀ (female)"]
  VOUT_GND = female pin header, 2 pins [form="♀ (female)"]
  J21 = female pin header, 16 pins [form="♀ (female)"]
  J22 = female pin header, 16 pins [form="♀ (female)"]
  SPI = female pin header, 3 pins [form="♀ (female)"]
  PWM = female pin header, 2 pins [form="♀ (female)"]

nets:
  GND: MBED.P$1, microSD_breakout.GND, Xbee.GND, Charger/Battery.pin2, Charger/Battery.pin4, J1.pin1, VOUT_GND.pin2
  N1: MBED.P$2, J1.pin10
  N2: MBED.P$5, microSD_breakout.DI, SPI.pin3
  N3: MBED.P$6, microSD_breakout.DO, SPI.pin2
  N4: MBED.P$7, microSD_breakout.SCK, SPI.pin1
  N5: MBED.P$8, microSD_breakout.CS
  N6: MBED.P$9, I2C.pin1
  N7: MBED.P$10, I2C.pin2
  N8: MBED.P$11, GPIO.pin1
  N9: MBED.P$12, GPIO.pin2
  N10: MBED.P$13, Serial.pin1
  N11: MBED.P$14, Serial.pin2
  N12: MBED.P$15, Analog_3.pin2
  N13: MBED.P$16, Analog_3.pin1
  N14: MBED.P$17, Analog.pin2
  N15: MBED.P$18, Analog.pin1
  N16: MBED.P$19, Analog_2.pin2
  N17: MBED.P$20, Analog_2.pin1
  N18: MBED.P$21, R1.Pin_1
  N19: MBED.P$22, R2.Pin_1
  N20: MBED.P$23, R3.Pin_1
  N21: MBED.P$24, PWM.pin1
  N22: MBED.P$25, PWM.pin2
  N23: MBED.P$26, Xbee.pin5
  N24: MBED.P$27, Xbee.pin2
  N25: MBED.P$28, Xbee.pin3
  N26: MBED.P$29, CAN.pin1
  N27: MBED.P$30, CAN.pin2
  VCC: MBED.P$40, microSD_breakout.VCC, Xbee.VCC, VOUT_GND.pin1
  N28: R3.Pin_0, J1.pin4
  N29: R2.Pin_0, J1.pin3
  N30: R1.Pin_0, J1.pin2
  N31: Charger/Battery.pin1, J1.pin7
  N32: Charger/Battery.pin3, J1.pin6
  N33: J2.pin1, J21.pin1
  N34: J2.pin2, J21.pin2
  N35: J2.pin3, J21.pin3
  N36: J2.pin4, J21.pin4
  N37: J2.pin5, J21.pin5
  N38: J2.pin6, J21.pin6
  N39: J2.pin7, J21.pin7
  N40: J2.pin8, J21.pin8
  N41: J2.pin9, J21.pin9
  N42: J2.pin10, J21.pin10
  N43: J2.pin11, J21.pin11
  N44: J2.pin12, J21.pin12
  N45: J2.pin13, J21.pin13
  N46: J2.pin14, J21.pin14
  N47: J2.pin15, J21.pin15
  N48: J2.pin16, J21.pin16
  N49: J3.pin1, J22.pin16
  N50: J3.pin2, J22.pin15
  N51: J3.pin3, J22.pin14
  N52: J3.pin4, J22.pin13
  N53: J3.pin5, J22.pin12
  N54: J3.pin6, J22.pin11
  N55: J3.pin7, J22.pin10
  N56: J3.pin8, J22.pin9
  N57: J3.pin9, J22.pin8
  N58: J3.pin10, J22.pin7
  N59: J3.pin11, J22.pin6
  N60: J3.pin12, J22.pin5
  N61: J3.pin13, J22.pin4
  N62: J3.pin14, J22.pin3
  N63: J3.pin15, J22.pin2
  N64: J3.pin16, J22.pin1

notes:
  5  6  7
  15 16
  17 18
  19 20
  24 25
  29 30
  9 10
  11 12
  13 14
  (No Interupts)
  (Out)
  (-)(+)(-)(+)
  VOUT GND
  Labels for SD's GND and VCC are flipped in schematic view
  Whitworth University
  Flight Computer
  Version 1.2
  June 2019
  Craig Russell
  06/14/19
